# Fritzing sketch irafan_rangkaian (saved by Fritzing 0.9.2b)

parts:
  Part1 = Arduino Mega ADK (Rev3)
  J1 = Basic Servo
  KY-1 = Keyes Relay [package=THT]
  LED1 = RGB LED (com. cathode, rbg) [package="5 mm [THT]"]
  DFPlayer_Mini1 = DFPlayer MINI [package="DIP (Dual Inline) [THT]"]
  SP1 = SPEAKER [package=pcb_mount_speaker]
  J2 = Piezo Speaker
  Keypad4x1 = Keypad Membran 4x4
  Display1 = LCD screen 16x2 IIC [part_number=101290]
  Part2 = RFID-RC522-v2
  U1 = MCP73831 [package=sot23-5]
  M1 = Pzem-004t
  Part3 = Coin Acceptor - 6-Coin version

nets:
  N1: Part1.D21/SCL, Display1.SCL
  N2: Part1.D20/SDA, Display1.SDA
  N3: Part1.D19/RX1, M1.TX
  N4: Part1.D18/TX1, M1.RX
  N5: Part1.D12_PWM, J1.pulse
  N6: Part1.D10_PWM, DFPlayer_Mini1.TX
  N7: Part1.D9_PWM, DFPlayer_Mini1.RX
  3V3: Part1.3V3, Part2.3.3V
  VCC: Part1.5V, J1.vcc, DFPlayer_Mini1.VCC, Display1.VCC, M1.5V
  GND: Part1.GND, J1.gnd, LED1.green_anode, Display1.GND, Part3.GND
  N8: Part1.D2_PWM, Part3.SIG
  N9: Part1.D5_PWM, Part2.RST
  N10: Part1.D6_PWM, KY-1.power
  N11: Part1.D7_PWM, J2.pin2
  N12: Part1.D23, Keypad4x1.Pin1
  N13: Part1.D25, Keypad4x1.Pin2
  N14: Part1.D27, Keypad4x1.Pin3
  N15: Part1.D29, Keypad4x1.Pin4
  N16: Part1.D31, Keypad4x1.Pin5
  N17: Part1.D33, Keypad4x1.Pin6
  N18: Part1.D35, Keypad4x1.Pin7
  N19: Part1.D37, Keypad4x1.Pin8
  N20: Part1.D39, LED1.red_anode
  N21: Part1.D41, LED1.common_cathode
  N22: Part1.D43, LED1.blue_anode
  N23: Part1.D46, U1.VSS
  N24: Part1.D47, U1.STAT
  N25: Part1.D50/MISO, Part2.MISO
  N26: Part1.D51/MOSI, Part2.MOSI
  N27: Part1.D52/SCK, Part2.SCK
  N28: Part1.D53/SS, Part2.SDA
  N29: DFPlayer_Mini1.SPK1, SP1.-
  N30: DFPlayer_Mini1.SPK2, SP1.+

custom parts:
  Keyes Relay: The Keyes 5V relay module is suitable for SCM development, home appliance control. It uses a 5V~12V TIL control signal which can control DC / AC signal.
  DFPlayer MINI: MP3 module by DFRobot.com for playing Music from an SD-Card. Supports WAV and MP3 files.
  Keypad Membran 4x4: Membrane Keypad 4x4 Matrix
  LCD screen 16x2 IIC: LCD screen with HD44780 controller enables showing text, symbols, value or anything else that comes from Croduino/Arduino. It is capable of showing 16 symbols in two lines and therefore can be used in many projects that need to send clearly visible and legible output information.. • Color of symbols: White • Backlight: Blue • Dimensions: 80 x 36 x 12 mm • Screen dimensions: 64.5 x 16 mm •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
  RFID-RC522-v2: A simple China made RFID-RC522 Reader; do check the pin labels, as this is a MFRC522 based clone.
  Pzem-004t: Pzem-004t used for measuring AC voltage, current, active power, frequency, power factor and active energy, the module is without display function, the data is read through the TTL interface.
  Coin Acceptor - 6-Coin version: 12V coin acceptor that can handle up to 6 different denominations. Output is either pulse width, serial, or single pin per coin value.
